# Fritzing sketch board-schematic (saved by Fritzing 0.9.3b)
circuit board: 7.5cm x 5.5cm
breadboards: 1

parts:
  TRIM_2 = TRIMPOT [package=3386u]
  TRIM_1 = TRIMPOT [package=3386u]
  LED1 = LED - 5mm [color="Red (633nm)" package="5 mm [THT]"]
  AUDIO_OUT = 3.5mm Audio Jack [package=audio-jack]
  TOGGLE = SPST Switch [package=switch-spdt_kit]
  FSR2 = female pin header, 2 pins [form="♀ (female)"]
  MPX_BREATH = female pin header, 6 pins [form="♀ (female)"]  # not connected
  Modern_Devices = female pin header, 6 pins [form="♀ (female)"]
  FSR1 = female pin header, 2 pins [form="♀ (female)"]
  5V = Screw terminal - 2 pins [package=THT]
  ON_/_OFF = SPST Switch [package=switch-spdt_lock.007s]
  R5 = Resistor [tolerance=±5% resistance=330 package=THT]
  R6 = Resistor [tolerance=±5% resistance=10k package=THT]
  R8 = Resistor [tolerance=±5% resistance=10k package=THT]
  USB_MIDI = female pin header, 5 pins [form="♀ (female)"]
  LM358 = LM358 [package=dip08]
  R9 = Resistor [tolerance=±5% resistance=5k package=THT]
  AINs = female pin header, 6 pins [form="♀ (female)"]
  USB2 = double row female pin header, 4 pins [form="♀ (female)"]  # not connected
  USB3 = double row female pin header, 4 pins [form="♀ (female)"]  # not connected
  USB4 = double row female pin header, 4 pins [form="♀ (female)"]  # not connected
  5V_2 = female pin header, 1 pin [form="♀ (female)"]
  USB5 = female pin header, 3 pins [form="♀ (female)"]
  GND = female pin header, 1 pin [form="♀ (female)"]
  BAT+ = female pin header, 1 pin [form="♀ (female)"]
  BAT- = female pin header, 1 pin [form="♀ (female)"]
  BTN = female pin header, 1 pin [form="♀ (female)"]
  BOOT = SWITCH-MOMENTARY-2 [package=tactile-pth-12mm]
  USB_BELA = female pin header, 4 pins [form="♀ (female)"]
  USB_GND = female pin header, 1 pin [form="♀ (female)"]
  USB_GND1 = female pin header, 1 pin [form="♀ (female)"]
  3V = female pin header, 1 pin [form="♀ (female)"]
  R7 = Resistor [tolerance=±5% resistance=1k package=THT]
  AINs1 = female pin header, 1 pin [form="♀ (female)"]
  R10 = Resistor [tolerance=±5% resistance=5k package=THT]

nets:
  N1: TRIM_2.CCW, TRIM_1.CCW, LED1.anode, R6.Pin_1, R8.Pin_1, LM358.G$1_V-, GND.pin1, BOOT.1, R7.Pin_1, R10.Pin_1
  N2: TRIM_2.WIPER, AINs.pin2
  N3: TRIM_2.CW, TRIM_1.CW, Modern_Devices.pin2, LM358.G$1_V+, R9.Pin_1, 5V_2.pin1
  N4: TRIM_1.WIPER, AINs.pin1
  N5: LED1.cathode, R5.Pin_1
  N6: AUDIO_OUT.RIGHT, USB5.pin3
  N7: AUDIO_OUT.SLEEVE, USB5.pin1
  N8: AUDIO_OUT.LEFT, USB5.pin2
  N9: TOGGLE.O, R7.Pin_0, AINs1.pin1
  N10: TOGGLE.P, FSR2.pin2, FSR1.pin2, 3V.pin1
  N11: FSR2.pin1, R8.Pin_0, AINs.pin4
  N12: Modern_Devices.pin1, USB_GND1.pin1
  N13: Modern_Devices.pin3, LM358.G$1_+IN, AINs.pin6
  N14: FSR1.pin1, R6.Pin_0, AINs.pin5
  N15: 5V.pin1, BAT-.pin1
  N16: 5V.pin2, ON_/_OFF.O
  N17: ON_/_OFF.P, BAT+.pin1
  N18: R5.Pin_0, LM358.G$1_OUT
  N19: USB_MIDI.pin1, USB_BELA.pin2
  N20: USB_MIDI.pin2, USB_BELA.pin1
  N21: USB_MIDI.pin4, USB_BELA.pin4
  N22: USB_MIDI.pin5, USB_GND.pin1
  N23: LM358.G$1_-IN, R9.Pin_0, R10.Pin_0
  N24: BTN.pin1, BOOT.2

notes:
  CCRMA
